# Fritzing sketch v3_current_control (saved by Fritzing 0.9.3b)
circuit board: 8cm x 4.5cm
breadboards: 1

parts:
  LM358 = LM 358 Dual Op-Amp [package="DIP8 [THT]"]
  C2 = Electrolytic Capacitor [capacitance=10µF package="100 mil [THT, electrolytic]"]  # not connected
  C3 = Electrolytic Capacitor [capacitance=10µF package="100 mil [THT, electrolytic]"]
  C4 = Capacitor [part_number=100p package=cap-pth-small2]
  C5 = Capacitor [part_number=100pf package=cap-pth-small2]
  R1 = Resistor [tolerance=±1% resistance=220k package="2010 [SMD]"]
  R6 = Resistor [tolerance=±1% resistance=220k package="2010 [SMD]"]
  R7 = Resistor [tolerance=±5% resistance=10k package="2010 [SMD]"]
  R8 = Resistor [tolerance=±5% resistance=10k package="2010 [SMD]"]
  MaxInput_(A1) = Header 2 [package=molex-1x2_lock]
  7805 = Voltage Regulator [package=to-220-alt]
  INA219 = INA219 High Side DC Current Sensor Breakout [part_number=904]
  C8 = Ceramic Capacitor [capacitance=100nF package="100 mil [THT, multilayer]"]
  Q1 = TRANSISTOR_NPN [package=to-92-ammo]
  R10 = Resistor [tolerance=±5% resistance=2k package="2010 [SMD]"]
  LED1 = LED - 3mm [color="Red (633nm)" package="3 mm [THT]"]
  CC_mode_(A2) = Header 2 [package=molex-1x2_lock]
  R11 = Resistor [tolerance=±5% resistance=10k package="2010 [SMD]"]
  R12 = Resistor [tolerance=±5% resistance=22k package="2010 [SMD]"]
  R13 = Resistor [tolerance=±5% resistance=1k package=THT]
  R14 = Resistor [tolerance=±5% resistance=100k package=THT]
  R15 = Resistor [tolerance=±5% resistance=15k package="2010 [SMD]"]
  D1 = Schottky Diode [part_number=1N5817 package="300 mil [THT]"]
  D2 = Schottky Diode [part_number=1N5817 package="300 mil [THT]"]
  R16 = Resistor [tolerance=±5% resistance=150k package="0603 [SMD]"]
  Vout = Header 2 [package=molex-1x2_lock]
  R17 = Resistor [tolerance=±5% resistance=15k package="0603 [SMD]"]
  U1 = POT [part_number="VV Pot" package=pot_alpha_rv16af-20]
  Feedback = Header 2 [package=molex-1x2_lock]

nets (from the schematic view):
  N1: LM358.connector0, LM358.connector4, R1.Pin_1, C8.1
  N2: LM358.connector1, R1.Pin_0, R7.Pin_1, C8.0
  N3: LM358.connector2, R6.Pin_1, R8.Pin_1
  GND: LM358.connector3, INA219.GND, Q1.E, R15.Pin_1, R16.Pin_1, R17.Pin_1
  N4: LM358.connector5, R13.Pin_1, R14.Pin_0
  N5: LM358.connector6, R11.Pin_0, R12.Pin_0, R14.Pin_1
  N6: LM358.connector7, C5.1, 7805.OUT, INA219.VCC, R10.Pin_0
  N7: C3.-, 7805.GND
  N8: C4.1, C4.2, 7805.IN
  N9: C5.2, R6.Pin_0
  N10: R7.Pin_0, INA219.VIN-
  N11: R8.Pin_0, INA219.VIN+
  N12: MaxInput_(A1).1, R13.Pin_0
  N13: Q1.B, R11.Pin_1
  N14: Q1.C, LED1.cathode, CC_mode_(A2).1
  N15: R10.Pin_1, LED1.anode
  N16: R12.Pin_1, R15.Pin_0, D1.anode
  N17: D1.cathode, D2.cathode, R16.Pin_0, Feedback.1
  N18: D2.anode, R17.Pin_0, U1.S
  N19: Vout.1, U1.E

notes:
  7.5v
  -5v
  CC mode

custom parts:
  INA219 High Side DC Current Sensor Breakout: This breakout board will solve all your power-monitoring problems. Instead of struggling with two multimeters, you can just use the handy INA219B chip on this breakout to both measure both the high side voltage and DC current draw over I2C with 1% precision. Most current-measuring devices such as our current panel meter are only good for low side measuring. That means that unless you want to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
